# Fritzing sketch circuit_bluetooth_module (saved by Fritzing 0.9.5d)
breadboards: 1

parts:
  Componente1 = Arduino Mega 2560 (Rev3)
  part = Resistor [tolerance=±5% resistance=1k package="2010 [SMD]"]
  part_2 = Resistor [tolerance=±5% resistance=1k package="2010 [SMD]"]
  part_3 = Resistor [tolerance=±5% resistance=1k package="2010 [SMD]"]
  Componente2 = Bluetooth HC-05

nets:
  5V: Componente1.5V, Componente2.VCC
  GND: Componente1.GND, part.Pin_0, Componente2.GND
  N1: Componente1.D0_RX0, Componente2.TXD
  N2: Componente1.D1_TX0, part_3.Pin_1
  N3: part.Pin_1, part_2.Pin_0
  N4: part_2.Pin_1, part_3.Pin_0, Componente2.RXD
